// Logisim project computer_clark.circ as structural Verilog
module pruebas_dispositivos (
  input  in_1,
  input  in_2,
  input  in_3,
  input  in_4,
  input  in_5
);

  wire dipswitch_1_p1, dipswitch_1_p2, dipswitch_1_p3, dipswitch_1_p4, dipswitch_1_p5, dipswitch_1_p6,
       dipswitch_1_p7, dipswitch_1_p8, dipswitch_2_p1, dipswitch_2_p2, dipswitch_2_p3, dipswitch_2_p4,
       dipswitch_2_p5, dipswitch_2_p6, dipswitch_2_p7, dipswitch_2_p8, mem_bit_1_out_3, mem_byte_1_out_10,
       mem_byte_1_out_11, mem_byte_1_out_12, mem_byte_1_out_13, mem_byte_1_out_14, mem_byte_1_out_15,
       mem_byte_1_out_16, mem_byte_1_out_17, register_nand_1_out_11, register_nand_1_out_12,
       register_nand_1_out_13, register_nand_1_out_14, register_nand_1_out_15, register_nand_1_out_16,
       register_nand_1_out_17, register_nand_1_out_18;

  // DipSwitch dipswitch_1: pin names not known; wires that end beside it: dipswitch_1_p1, dipswitch_1_p2, dipswitch_1_p3, dipswitch_1_p4, dipswitch_1_p5, dipswitch_1_p6, dipswitch_1_p7, dipswitch_1_p8
  LED led_1 (.in(mem_bit_1_out_3));
  mem_bit mem_bit_1 (.in_2(in_2), .in_1(in_1), .out_3(mem_bit_1_out_3));
  LedBar ledbar_1 (
    .led0(register_nand_1_out_11), .led1(register_nand_1_out_12), .led2(register_nand_1_out_13),
    .led3(register_nand_1_out_14), .led4(register_nand_1_out_15), .led5(register_nand_1_out_16),
    .led6(register_nand_1_out_17), .led7(register_nand_1_out_18));
  register_nand register_nand_1 (
    .in_1(dipswitch_1_p1), .in_2(dipswitch_1_p2), .in_3(dipswitch_1_p3), .in_4(dipswitch_1_p4),
    .in_5(dipswitch_1_p5), .in_6(dipswitch_1_p6), .in_7(dipswitch_1_p7), .in_8(dipswitch_1_p8), .in_9(in_4),
    .in_10(in_5), .out_11(register_nand_1_out_11), .out_12(register_nand_1_out_12),
    .out_13(register_nand_1_out_13), .out_14(register_nand_1_out_14), .out_15(register_nand_1_out_15),
    .out_16(register_nand_1_out_16), .out_17(register_nand_1_out_17), .out_18(register_nand_1_out_18));
  // DipSwitch dipswitch_2: pin names not known; wires that end beside it: dipswitch_2_p1, dipswitch_2_p2, dipswitch_2_p3, dipswitch_2_p4, dipswitch_2_p5, dipswitch_2_p6, dipswitch_2_p7, dipswitch_2_p8
  mem_byte mem_byte_1 (
    .in_9(in_3), .in_2(dipswitch_2_p2), .in_3(dipswitch_2_p3), .in_4(dipswitch_2_p4), .in_5(dipswitch_2_p5),
    .in_6(dipswitch_2_p6), .in_7(dipswitch_2_p7), .in_8(dipswitch_2_p8), .in_1(dipswitch_2_p1),
    .out_11(mem_byte_1_out_11), .out_12(mem_byte_1_out_12), .out_13(mem_byte_1_out_13),
    .out_14(mem_byte_1_out_14), .out_15(mem_byte_1_out_15), .out_16(mem_byte_1_out_16),
    .out_17(mem_byte_1_out_17), .out_10(mem_byte_1_out_10));
  LedBar ledbar_2 (
    .led0(mem_byte_1_out_10), .led1(mem_byte_1_out_11), .led2(mem_byte_1_out_12), .led3(mem_byte_1_out_13),
    .led4(mem_byte_1_out_14), .led5(mem_byte_1_out_15), .led6(mem_byte_1_out_16), .led7(mem_byte_1_out_17));

  // Notes on the sheet:
  //   Memoria de 1 bit
  //   Registro de 1 byte
  //   Memoria de 1 byte
endmodule

module register_nand (
  input  in_1,
  input  in_2,
  input  in_3,
  input  in_4,
  input  in_5,
  input  in_6,
  input  in_7,
  input  in_8,
  input  in_9,
  input  in_10,
  output out_11,
  output out_12,
  output out_13,
  output out_14,
  output out_15,
  output out_16,
  output out_17,
  output out_18
);

  wire mem_byte_1_out_10, mem_byte_1_out_11, mem_byte_1_out_12, mem_byte_1_out_13, mem_byte_1_out_14,
       mem_byte_1_out_15, mem_byte_1_out_16, mem_byte_1_out_17;

  LED led_1 (.in(mem_byte_1_out_10));
  mem_byte mem_byte_1 (
    .in_9(in_9), .in_2(in_2), .in_3(in_3), .in_4(in_4), .in_5(in_5), .in_6(in_6), .in_7(in_7), .in_8(in_8),
    .in_1(in_1), .out_11(mem_byte_1_out_11), .out_12(mem_byte_1_out_12), .out_13(mem_byte_1_out_13),
    .out_14(mem_byte_1_out_14), .out_15(mem_byte_1_out_15), .out_16(mem_byte_1_out_16),
    .out_17(mem_byte_1_out_17), .out_10(mem_byte_1_out_10));
  LED led_2 (.in(mem_byte_1_out_11));
  LED led_3 (.in(mem_byte_1_out_12));
  LED led_4 (.in(mem_byte_1_out_13));
  LED led_5 (.in(mem_byte_1_out_14));
  LED led_6 (.in(mem_byte_1_out_15));
  LED led_7 (.in(mem_byte_1_out_16));
  LED led_8 (.in(mem_byte_1_out_17));
  enabler_nand enabler_nand_1 (
    .in_2(mem_byte_1_out_11), .in_3(mem_byte_1_out_12), .in_4(mem_byte_1_out_13), .in_5(mem_byte_1_out_14),
    .in_6(mem_byte_1_out_15), .in_7(mem_byte_1_out_16), .in_8(mem_byte_1_out_17), .in_1(mem_byte_1_out_10),
    .in_9(in_10), .out_11(out_12), .out_12(out_13), .out_13(out_14), .out_14(out_15), .out_15(out_16),
    .out_16(out_17), .out_17(out_18), .out_10(out_11));
endmodule

module enabler_nand (
  input  in_1,
  input  in_2,
  input  in_3,
  input  in_4,
  input  in_5,
  input  in_6,
  input  in_7,
  input  in_8,
  input  in_9,
  output out_10,
  output out_11,
  output out_12,
  output out_13,
  output out_14,
  output out_15,
  output out_16,
  output out_17
);

  and_nand and_nand_1 (.in_1(in_1), .in_2(in_9), .out_3(out_10));
  and_nand and_nand_2 (.in_1(in_2), .in_2(in_9), .out_3(out_11));
  and_nand and_nand_3 (.in_1(in_3), .in_2(in_9), .out_3(out_12));
  and_nand and_nand_4 (.in_1(in_4), .in_2(in_9), .out_3(out_13));
  and_nand and_nand_5 (.in_1(in_5), .in_2(in_9), .out_3(out_14));
  and_nand and_nand_6 (.in_1(in_6), .in_2(in_9), .out_3(out_15));
  and_nand and_nand_7 (.in_1(in_7), .in_2(in_9), .out_3(out_16));
  and_nand and_nand_8 (.in_1(in_8), .in_2(in_9), .out_3(out_17));

  // Notes on the sheet:
  //   input
  //   enabler
  //   output
endmodule

module mem_byte (
  input  in_1,
  input  in_2,
  input  in_3,
  input  in_4,
  input  in_5,
  input  in_6,
  input  in_7,
  input  in_8,
  input  in_9,
  output out_10,
  output out_11,
  output out_12,
  output out_13,
  output out_14,
  output out_15,
  output out_16,
  output out_17
);

  mem_bit mem_bit_1 (.in_2(in_9), .in_1(in_1), .out_3(out_10));
  mem_bit mem_bit_2 (.in_2(in_9), .in_1(in_2), .out_3(out_11));
  mem_bit mem_bit_3 (.in_2(in_9), .in_1(in_3), .out_3(out_12));
  mem_bit mem_bit_4 (.in_2(in_9), .in_1(in_4), .out_3(out_13));
  mem_bit mem_bit_5 (.in_2(in_9), .in_1(in_5), .out_3(out_14));
  mem_bit mem_bit_6 (.in_2(in_9), .in_1(in_6), .out_3(out_15));
  mem_bit mem_bit_7 (.in_2(in_9), .in_1(in_7), .out_3(out_16));
  mem_bit mem_bit_8 (.in_2(in_9), .in_1(in_8), .out_3(out_17));

  // Notes on the sheet:
  //   input
  //   set
  //   output
endmodule

module mem_bit (
  input  in_1,
  input  in_2,
  output out_3
);

  wire nand_transistors_1_out_3, nand_transistors_2_out_3, nand_transistors_4_out_3, or_nand_1_out_3,
       por_1_out;

  POR #(.PorHighDuration(1)) por_1 (.out(por_1_out));
  or_nand or_nand_1 (.in_1(in_2), .in_2(por_1_out), .out_3(or_nand_1_out_3));
  nand_transistors nand_transistors_1 (.in_1(in_1), .in_2(or_nand_1_out_3), .out_3(nand_transistors_1_out_3));
  nand_transistors nand_transistors_2 (
    .in_1(nand_transistors_1_out_3), .in_2(or_nand_1_out_3), .out_3(nand_transistors_2_out_3));
  nand_transistors nand_transistors_3 (.in_1(nand_transistors_1_out_3), .in_2(nand_transistors_4_out_3), .out_3(out_3));
  nand_transistors nand_transistors_4 (.in_1(out_3), .in_2(nand_transistors_2_out_3), .out_3(nand_transistors_4_out_3));

  // Notes on the sheet:
  //   in_2: pull=up
endmodule

module or_nand (
  input  in_1,
  input  in_2,
  output out_3
);

  wire not_nand_1_out_2, not_nand_2_out_2;

  not_nand not_nand_1 (.in_1(in_1), .out_2(not_nand_1_out_2));
  not_nand not_nand_2 (.in_1(in_2), .out_2(not_nand_2_out_2));
  nand_transistors nand_transistors_1 (.in_1(not_nand_1_out_2), .in_2(not_nand_2_out_2), .out_3(out_3));
endmodule

module and_nand (
  input  in_1,
  input  in_2,
  output out_3
);

  wire nand_transistors_1_out_3;

  nand_transistors nand_transistors_1 (.in_1(in_1), .in_2(in_2), .out_3(nand_transistors_1_out_3));
  not_nand not_nand_1 (.in_1(nand_transistors_1_out_3), .out_2(out_3));
endmodule

module not_nand (
  input  in_1,
  output out_2
);

  nand_transistors nand_transistors_1 (.in_1(in_1), .in_2(in_1), .out_3(out_2));
endmodule

module nand_transistors (
  input  in_1,
  input  in_2,
  output out_3
);

  wire transistor_1_out;

  Pull_Resistor #(.pull(1)) pull_resistor_1 ();  // open: node
  Transistor #(.\type ("n")) transistor_1 (.in(1'b0), .out(transistor_1_out), .gate(in_1));
  Transistor #(.\type ("n")) transistor_2 (.in(transistor_1_out), .out(out_3), .gate(in_2));
  Pull_Resistor #(.pull(1)) pull_resistor_2 (.node(out_3));

  // Notes on the sheet:
  //   in_2: initial=0x1
endmodule
